// Logisim project CPU8b.circ as structural Verilog: 21 circuits, main circuit main
module main (
  input  clear,
  input  in_2
);

  wire alu_1_t, clock_1_out, control_unit_13fa0f51_1_branch, control_unit_13fa0f51_1_is_imm,
       control_unit_13fa0f51_1_jsr, control_unit_13fa0f51_1_jump, control_unit_13fa0f51_1_pc_load,
       control_unit_13fa0f51_1_ram_load, control_unit_13fa0f51_1_ram_to_reg, control_unit_13fa0f51_1_ram_wri,
       control_unit_13fa0f51_1_ret, control_unit_13fa0f51_1_unsigned_signed_dba66f78,
       control_unit_13fa0f51_1_wrien, decoder_1_out0, decoder_1_out1, decoder_1_out2, decoder_1_out3,
       decoder_1_out4, decoder_1_out5, decoder_1_out6, decoder_1_out7, decoder_1_out8, decoder_1_out9,
       decoder_1_out10, decoder_1_out11, decoder_1_out12, decoder_1_out13, decoder_1_out14, decoder_1_out15,
       decoder_1_out16, decoder_1_out17, decoder_1_out18, decoder_1_out19, decoder_1_out20, decoder_1_out21,
       decoder_1_out22, decoder_1_out23, decoder_1_out24, decoder_1_out25, decoder_1_out26, decoder_1_out27,
       decoder_1_out28, decoder_1_out29, decoder_1_out30, decoder_1_out31, enter_out, i0_out, i1_out, i2_out,
       i3_out, i4_out, i5_out, i6_out, i7_out, i8_out, i9_out;
  wire [2:0] control_unit_13fa0f51_1_alu_opcode_0dd9a30d, control_unit_13fa0f51_1_alu_shamt_1da623f9,
       control_unit_13fa0f51_1_cond, control_unit_13fa0f51_1_readaddra, control_unit_13fa0f51_1_readaddrb,
       control_unit_13fa0f51_1_wriaddr;
  wire [4:0] bit_extender_1_out;
  wire [7:0] alu_1_result, bcd_1_data, control_unit_13fa0f51_1_imm, displayram_1_addr, displayram_1_ascii,
       multiplexer_1_out, multiplexer_2_out, pc_1_out_10, ram_1_dout, register_file_ff49ba11_1_douta,
       register_file_ff49ba11_1_doutb;
  wire [31:0] rom_1_data;
  wire [39:0] ascii_1_out_2;

  control_unit_13fa0f51 control_unit_13fa0f51_1 (
    .in_1(rom_1_data), .T(alu_1_t), .Jump(control_unit_13fa0f51_1_jump),
    .Branch(control_unit_13fa0f51_1_branch), .RET(control_unit_13fa0f51_1_ret),
    .JSR(control_unit_13fa0f51_1_jsr), .PC_load(control_unit_13fa0f51_1_pc_load),
    .WriAddr(control_unit_13fa0f51_1_wriaddr), .ReadAddrA(control_unit_13fa0f51_1_readaddra),
    .ReadAddrB(control_unit_13fa0f51_1_readaddrb), .WriEn(control_unit_13fa0f51_1_wrien),
    .ALU_shamt_1da623f9(control_unit_13fa0f51_1_alu_shamt_1da623f9),
    .ALU_opcode_0dd9a30d(control_unit_13fa0f51_1_alu_opcode_0dd9a30d),
    .UnSigned_Signed_dba66f78(control_unit_13fa0f51_1_unsigned_signed_dba66f78),
    .COND(control_unit_13fa0f51_1_cond), .Imm(control_unit_13fa0f51_1_imm),
    .is_imm(control_unit_13fa0f51_1_is_imm), .RAM_Wri(control_unit_13fa0f51_1_ram_wri),
    .RAM_load(control_unit_13fa0f51_1_ram_load), .RAM_to_Reg(control_unit_13fa0f51_1_ram_to_reg));
  Clock clock_1 (.out(clock_1_out));
  displayRAM displayram_1 (
    .clock(clock_1_out), .Clear(clear), .RAM_Wri(control_unit_13fa0f51_1_ram_wri), .Adress(alu_1_result),
    .DataB(register_file_ff49ba11_1_doutb), .Addr(displayram_1_addr), .ASCII(displayram_1_ascii));
  PC pc_1 (
    .Jump(control_unit_13fa0f51_1_jump), .Branch(control_unit_13fa0f51_1_branch), .Clk(clock_1_out),
    .PC_load_028894c1(control_unit_13fa0f51_1_pc_load), .clear(clear), .RET(control_unit_13fa0f51_1_ret),
    .JSR(control_unit_13fa0f51_1_jsr), .offest(control_unit_13fa0f51_1_imm),
    .Imm(control_unit_13fa0f51_1_imm), .out_10(pc_1_out_10));
  ASCII ascii_1 (.in_1(displayram_1_ascii), .out_2(ascii_1_out_2));
  Bit_Extender #(.out_width(5), .\type ("zero")) bit_extender_1 (.in(displayram_1_addr), .out(bit_extender_1_out));
  ROM #(.dataWidth(32)) rom_1 (.addr(pc_1_out_10), .data(rom_1_data));
  BCD bcd_1 (
    .i0(i0_out), .i1(i1_out), .i2(i2_out), .i3(i3_out), .i4(i4_out), .i5(i5_out), .i6(i6_out), .i7(i7_out),
    .i8(i8_out), .i9(i9_out), .Add(in_2), .Sub(in_2), .Mul(in_2), .Div(in_2), .enter(enter_out),
    .Clear(clear), .data(bcd_1_data));  // open: is_number, is_operate, addr
  Button i0 (.out(i0_out));
  Button i1 (.out(i1_out));
  register_file_ff49ba11 register_file_ff49ba11_1 (
    .WriAddr(control_unit_13fa0f51_1_wriaddr), .IO(bcd_1_data), .From_keyBoard(enter_out),
    .WriEn(control_unit_13fa0f51_1_wrien), .Clock(clock_1_out), .ClearAll(clear), .Din(multiplexer_2_out),
    .readAddrA(control_unit_13fa0f51_1_readaddra), .readAddrB(control_unit_13fa0f51_1_readaddrb),
    .DoutA(register_file_ff49ba11_1_douta), .DoutB(register_file_ff49ba11_1_doutb));
  Button i2 (.out(i2_out));
  Button i3 (.out(i3_out));
  Button i4 (.out(i4_out));
  Button i5 (.out(i5_out));
  Multiplexer #(.width(8)) multiplexer_1 (
    .in0(register_file_ff49ba11_1_doutb), .in1(control_unit_13fa0f51_1_imm), .out(multiplexer_1_out),
    .sel(control_unit_13fa0f51_1_is_imm));
  Button i7 (.out(i7_out));
  Button i6 (.out(i6_out));
  ALU alu_1 (
    .shamt(control_unit_13fa0f51_1_alu_shamt_1da623f9), .opcode(control_unit_13fa0f51_1_alu_opcode_0dd9a30d),
    .unsign_sign_8fb0702b(control_unit_13fa0f51_1_unsigned_signed_dba66f78),
    .A(register_file_ff49ba11_1_douta), .B(multiplexer_1_out),
    .COND_0_1NOT_2_3_4_5_6_ve_7_ve_39ad1e93(control_unit_13fa0f51_1_cond), .T(alu_1_t), .result(alu_1_result));
  Button i8 (.out(i8_out));
  Button i9 (.out(i9_out));
  Button enter (.out(enter_out));
  RAM #(.clearpin("true"), .databus("bibusControlled"), .readbehav("war"), .trigger("falling")) ram_1 (
    .addr(alu_1_result), .we(control_unit_13fa0f51_1_ram_wri), .oe(control_unit_13fa0f51_1_ram_load),
    .clk(clock_1_out), .din(register_file_ff49ba11_1_doutb), .dout(ram_1_dout), .clr(clear));
  Decoder #(.enable("false"), .select(5)) decoder_1 (
    .out0(decoder_1_out0), .out1(decoder_1_out1), .out2(decoder_1_out2), .out3(decoder_1_out3),
    .out4(decoder_1_out4), .out5(decoder_1_out5), .out6(decoder_1_out6), .out7(decoder_1_out7),
    .out8(decoder_1_out8), .out9(decoder_1_out9), .out10(decoder_1_out10), .out11(decoder_1_out11),
    .out12(decoder_1_out12), .out13(decoder_1_out13), .out14(decoder_1_out14), .out15(decoder_1_out15),
    .out16(decoder_1_out16), .out17(decoder_1_out17), .out18(decoder_1_out18), .out19(decoder_1_out19),
    .out20(decoder_1_out20), .out21(decoder_1_out21), .out22(decoder_1_out22), .out23(decoder_1_out23),
    .out24(decoder_1_out24), .out25(decoder_1_out25), .out26(decoder_1_out26), .out27(decoder_1_out27),
    .out28(decoder_1_out28), .out29(decoder_1_out29), .out30(decoder_1_out30), .out31(decoder_1_out31),
    .sel(bit_extender_1_out));
  Multiplexer #(.width(8)) multiplexer_2 (
    .in0(alu_1_result), .in1(ram_1_dout), .out(multiplexer_2_out), .sel(control_unit_13fa0f51_1_ram_to_reg));
  word word_1 (.in_1(ascii_1_out_2), .Wri(decoder_1_out0), .Clock(clock_1_out), .Clear(clear));
  word word_2 (.in_1(ascii_1_out_2), .Wri(decoder_1_out10), .Clock(clock_1_out), .Clear(clear));
  word word_3 (.in_1(ascii_1_out_2), .Wri(decoder_1_out20), .Clock(clock_1_out), .Clear(clear));
  word word_4 (.in_1(ascii_1_out_2), .Wri(decoder_1_out30), .Clock(clock_1_out), .Clear(clear));
  word word_5 (.in_1(ascii_1_out_2), .Wri(decoder_1_out1), .Clock(clock_1_out), .Clear(clear));
  word word_6 (.in_1(ascii_1_out_2), .Wri(decoder_1_out11), .Clock(clock_1_out), .Clear(clear));
  word word_7 (.in_1(ascii_1_out_2), .Wri(decoder_1_out21), .Clock(clock_1_out), .Clear(clear));
  word word_8 (.in_1(ascii_1_out_2), .Wri(decoder_1_out31), .Clock(clock_1_out), .Clear(clear));
  word word_9 (.in_1(ascii_1_out_2), .Wri(decoder_1_out2), .Clock(clock_1_out), .Clear(clear));
  word word_10 (.in_1(ascii_1_out_2), .Wri(decoder_1_out12), .Clock(clock_1_out), .Clear(clear));
  word word_11 (.in_1(ascii_1_out_2), .Wri(decoder_1_out22), .Clock(clock_1_out), .Clear(clear));
  word word_12 (.in_1(ascii_1_out_2), .Wri(decoder_1_out3), .Clock(clock_1_out), .Clear(clear));
  word word_13 (.in_1(ascii_1_out_2), .Wri(decoder_1_out13), .Clock(clock_1_out), .Clear(clear));
  word word_14 (.in_1(ascii_1_out_2), .Wri(decoder_1_out23), .Clock(clock_1_out), .Clear(clear));
  word word_15 (.in_1(ascii_1_out_2), .Wri(decoder_1_out4), .Clock(clock_1_out), .Clear(clear));
  word word_16 (.in_1(ascii_1_out_2), .Wri(decoder_1_out14), .Clock(clock_1_out), .Clear(clear));
  word word_17 (.in_1(ascii_1_out_2), .Wri(decoder_1_out24), .Clock(clock_1_out), .Clear(clear));
  word word_18 (.in_1(ascii_1_out_2), .Wri(decoder_1_out5), .Clock(clock_1_out), .Clear(clear));
  word word_19 (.in_1(ascii_1_out_2), .Wri(decoder_1_out15), .Clock(clock_1_out), .Clear(clear));
  word word_20 (.in_1(ascii_1_out_2), .Wri(decoder_1_out25), .Clock(clock_1_out), .Clear(clear));
  word word_21 (.in_1(ascii_1_out_2), .Wri(decoder_1_out6), .Clock(clock_1_out), .Clear(clear));
  word word_22 (.in_1(ascii_1_out_2), .Wri(decoder_1_out16), .Clock(clock_1_out), .Clear(clear));
  word word_23 (.in_1(ascii_1_out_2), .Wri(decoder_1_out26), .Clock(clock_1_out), .Clear(clear));
  word word_24 (.in_1(ascii_1_out_2), .Wri(decoder_1_out7), .Clock(clock_1_out), .Clear(clear));
  word word_25 (.in_1(ascii_1_out_2), .Wri(decoder_1_out17), .Clock(clock_1_out), .Clear(clear));
  word word_26 (.in_1(ascii_1_out_2), .Wri(decoder_1_out27), .Clock(clock_1_out), .Clear(clear));
  word word_27 (.in_1(ascii_1_out_2), .Wri(decoder_1_out8), .Clock(clock_1_out), .Clear(clear));
  word word_28 (.in_1(ascii_1_out_2), .Wri(decoder_1_out18), .Clock(clock_1_out), .Clear(clear));
  word word_29 (.in_1(ascii_1_out_2), .Wri(decoder_1_out28), .Clock(clock_1_out), .Clear(clear));
  word word_30 (.in_1(ascii_1_out_2), .Wri(decoder_1_out9), .Clock(clock_1_out), .Clear(clear));
  word word_31 (.in_1(ascii_1_out_2), .Wri(decoder_1_out19), .Clock(clock_1_out), .Clear(clear));
  word word_32 (.in_1(ascii_1_out_2), .Wri(decoder_1_out29), .Clock(clock_1_out), .Clear(clear));

  // Notes on the sheet:
  //   contents of rom_1 (hex, n*v repeats v):
  //   e0000003 1c023fd6 dc000001 20000003 40000003 60000003 80001903 1a028110 da020000 24000041 1c8
  //   80000283 1a028110 da020000 48000041 308 78000001 803fc5 1003fc5 1803fc5 c0000003 8
endmodule

module FA (
  input  A,
  input  B,
  input  Cin,
  output sum,
  output Cout
);

  wire and_1_out, and_2_out, xor_1_out;

  xor xor_1 (xor_1_out, A, B);
  and and_1 (and_1_out, B, A);
  xor xor_2 (sum, xor_1_out, Cin);
  and and_2 (and_2_out, xor_1_out, Cin);
  or or_1 (Cout, and_2_out, and_1_out);
endmodule

module adder_8b_da2f1a56 (
  input  [7:0] A,
  input  [7:0] B,
  input  Sub,
  output Zero,
  output L_VE_73f3d2a1,
  output Carry,
  output Overflow,
  output [7:0] out_8
);

  wire fa_2_cout, fa_3_cout, fa_4_cout, fa_5_cout, fa_6_cout, fa_7_cout, fa_8_cout, xor_1_out, xor_2_out,
       xor_3_out, xor_4_out, xor_5_out, xor_6_out, xor_7_out, xor_8_out;

  FA fa_1 (.A(A[7]), .B(xor_1_out), .Cin(fa_2_cout), .sum(L_VE_73f3d2a1), .Cout(Carry));
  xor xor_1 (xor_1_out, B[7], Sub);
  FA fa_2 (.A(A[6]), .B(xor_2_out), .Cin(fa_3_cout), .sum(out_8[6]), .Cout(fa_2_cout));
  xor xor_2 (xor_2_out, B[6], Sub);
  FA fa_3 (.A(A[5]), .B(xor_3_out), .Cin(fa_4_cout), .sum(out_8[5]), .Cout(fa_3_cout));
  xor xor_3 (xor_3_out, B[5], Sub);
  FA fa_4 (.A(A[4]), .B(xor_4_out), .Cin(fa_5_cout), .sum(out_8[4]), .Cout(fa_4_cout));
  xor xor_4 (xor_4_out, B[4], Sub);
  FA fa_5 (.A(A[3]), .B(xor_5_out), .Cin(fa_6_cout), .sum(out_8[3]), .Cout(fa_5_cout));
  xor xor_5 (xor_5_out, B[3], Sub);
  FA fa_6 (.A(A[2]), .B(xor_6_out), .Cin(fa_7_cout), .sum(out_8[2]), .Cout(fa_6_cout));
  xor xor_6 (xor_6_out, B[2], Sub);
  FA fa_7 (.A(A[1]), .B(xor_7_out), .Cin(fa_8_cout), .sum(out_8[1]), .Cout(fa_7_cout));
  xor xor_7 (xor_7_out, B[1], Sub);
  FA fa_8 (.A(A[0]), .B(xor_8_out), .Cin(Sub), .sum(out_8[0]), .Cout(fa_8_cout));
  xor xor_8 (xor_8_out, B[0], Sub);
  xor xor_9 (Overflow, Carry, fa_2_cout);
  nor nor_1 (Zero, L_VE_73f3d2a1, out_8[6], out_8[5], out_8[4], out_8[3], out_8[2], out_8[1], out_8[0]);

  assign out_8[7] = L_VE_73f3d2a1;
endmodule

module XOR_8b_18f17b81 (
  input  [7:0] in_1,
  input  [7:0] in_2,
  output [7:0] out_3
);

  xor xor_1 (out_3[7], in_2[7], in_1[7]);
  xor xor_2 (out_3[6], in_2[6], in_1[6]);
  xor xor_3 (out_3[5], in_2[5], in_1[5]);
  xor xor_4 (out_3[4], in_2[4], in_1[4]);
  xor xor_5 (out_3[3], in_2[3], in_1[3]);
  xor xor_6 (out_3[2], in_2[2], in_1[2]);
  xor xor_7 (out_3[1], in_2[1], in_1[1]);
  xor xor_8 (out_3[0], in_2[0], in_1[0]);
endmodule

module AND_8b_6958ddab (
  input  [7:0] in_1,
  input  [7:0] in_2,
  output [7:0] out_3
);

  and and_1 (out_3[7], in_2[7], in_1[7]);
  and and_2 (out_3[6], in_2[6], in_1[6]);
  and and_3 (out_3[5], in_2[5], in_1[5]);
  and and_4 (out_3[4], in_2[4], in_1[4]);
  and and_5 (out_3[3], in_2[3], in_1[3]);
  and and_6 (out_3[2], in_2[2], in_1[2]);
  and and_7 (out_3[1], in_2[1], in_1[1]);
  and and_8 (out_3[0], in_2[0], in_1[0]);
endmodule

module OR_8b_d5c0bf99 (
  input  [7:0] in_1,
  input  [7:0] in_2,
  output [7:0] out_3
);

  or or_1 (out_3[7], in_2[7], in_1[7]);
  or or_2 (out_3[6], in_2[6], in_1[6]);
  or or_3 (out_3[5], in_2[5], in_1[5]);
  or or_4 (out_3[4], in_2[4], in_1[4]);
  or or_5 (out_3[3], in_2[3], in_1[3]);
  or or_6 (out_3[2], in_2[2], in_1[2]);
  or or_7 (out_3[1], in_2[1], in_1[1]);
  or or_8 (out_3[0], in_2[0], in_1[0]);
endmodule

module right_shift_8b_d6623a56 (
  input  [7:0] in_1,
  input  Arithmetic,
  input  [2:0] shamt,
  output [7:0] out_4
);

  wire multiplexer_1_out, multiplexer_2_out, multiplexer_3_out, multiplexer_4_out, multiplexer_5_out,
       multiplexer_6_out, multiplexer_7_out, multiplexer_8_out, multiplexer_9_out, multiplexer_10_out,
       multiplexer_11_out, multiplexer_12_out, multiplexer_13_out, multiplexer_14_out, multiplexer_15_out,
       multiplexer_16_out, multiplexer_17_out;

  Multiplexer multiplexer_1 (.in0(1'b0), .in1(in_1[7]), .out(multiplexer_1_out), .sel(Arithmetic));
  Multiplexer multiplexer_2 (.in0(in_1[0]), .in1(in_1[1]), .out(multiplexer_2_out), .sel(shamt[0]));
  Multiplexer multiplexer_3 (.in0(in_1[1]), .in1(in_1[2]), .out(multiplexer_3_out), .sel(shamt[0]));
  Multiplexer multiplexer_4 (.in0(in_1[2]), .in1(in_1[3]), .out(multiplexer_4_out), .sel(shamt[0]));
  Multiplexer multiplexer_5 (.in0(in_1[3]), .in1(in_1[4]), .out(multiplexer_5_out), .sel(shamt[0]));
  Multiplexer multiplexer_6 (.in0(in_1[4]), .in1(in_1[5]), .out(multiplexer_6_out), .sel(shamt[0]));
  Multiplexer multiplexer_7 (.in0(in_1[5]), .in1(in_1[6]), .out(multiplexer_7_out), .sel(shamt[0]));
  Multiplexer multiplexer_8 (.in0(in_1[6]), .in1(in_1[7]), .out(multiplexer_8_out), .sel(shamt[0]));
  Multiplexer multiplexer_9 (.in0(in_1[7]), .in1(multiplexer_1_out), .out(multiplexer_9_out), .sel(shamt[0]));
  Multiplexer multiplexer_10 (
    .in0(multiplexer_2_out), .in1(multiplexer_4_out), .out(multiplexer_10_out), .sel(shamt[1]));
  Multiplexer multiplexer_11 (
    .in0(multiplexer_3_out), .in1(multiplexer_5_out), .out(multiplexer_11_out), .sel(shamt[1]));
  Multiplexer multiplexer_12 (
    .in0(multiplexer_4_out), .in1(multiplexer_6_out), .out(multiplexer_12_out), .sel(shamt[1]));
  Multiplexer multiplexer_13 (
    .in0(multiplexer_5_out), .in1(multiplexer_7_out), .out(multiplexer_13_out), .sel(shamt[1]));
  Multiplexer multiplexer_14 (
    .in0(multiplexer_6_out), .in1(multiplexer_8_out), .out(multiplexer_14_out), .sel(shamt[1]));
  Multiplexer multiplexer_15 (
    .in0(multiplexer_7_out), .in1(multiplexer_9_out), .out(multiplexer_15_out), .sel(shamt[1]));
  Multiplexer multiplexer_16 (
    .in0(multiplexer_8_out), .in1(multiplexer_1_out), .out(multiplexer_16_out), .sel(shamt[1]));
  Multiplexer multiplexer_17 (
    .in0(multiplexer_9_out), .in1(multiplexer_1_out), .out(multiplexer_17_out), .sel(shamt[1]));
  Multiplexer multiplexer_18 (.in0(multiplexer_10_out), .in1(multiplexer_14_out), .out(out_4[0]), .sel(shamt[2]));
  Multiplexer multiplexer_19 (.in0(multiplexer_11_out), .in1(multiplexer_15_out), .out(out_4[1]), .sel(shamt[2]));
  Multiplexer multiplexer_20 (.in0(multiplexer_12_out), .in1(multiplexer_16_out), .out(out_4[2]), .sel(shamt[2]));
  Multiplexer multiplexer_21 (.in0(multiplexer_13_out), .in1(multiplexer_17_out), .out(out_4[3]), .sel(shamt[2]));
  Multiplexer multiplexer_22 (.in0(multiplexer_14_out), .in1(multiplexer_1_out), .out(out_4[4]), .sel(shamt[2]));
  Multiplexer multiplexer_23 (.in0(multiplexer_15_out), .in1(multiplexer_1_out), .out(out_4[5]), .sel(shamt[2]));
  Multiplexer multiplexer_24 (.in0(multiplexer_16_out), .in1(multiplexer_1_out), .out(out_4[6]), .sel(shamt[2]));
  Multiplexer multiplexer_25 (.in0(multiplexer_17_out), .in1(multiplexer_1_out), .out(out_4[7]), .sel(shamt[2]));
endmodule

module left_shift_8b_5403b38f (
  input  [7:0] in_1,
  input  Arithmetic,
  input  [2:0] shamt,
  output [7:0] out_4
);

  wire multiplexer_1_out, multiplexer_2_out, multiplexer_3_out, multiplexer_4_out, multiplexer_5_out,
       multiplexer_6_out, multiplexer_7_out, multiplexer_8_out, multiplexer_9_out, multiplexer_10_out,
       multiplexer_11_out, multiplexer_12_out, multiplexer_13_out, multiplexer_14_out, multiplexer_15_out,
       multiplexer_16_out, multiplexer_17_out;

  Multiplexer multiplexer_1 (.in0(1'b0), .in1(in_1[0]), .out(multiplexer_1_out), .sel(Arithmetic));
  Multiplexer multiplexer_2 (.in0(in_1[7]), .in1(in_1[6]), .out(multiplexer_2_out), .sel(shamt[0]));
  Multiplexer multiplexer_3 (.in0(in_1[6]), .in1(in_1[5]), .out(multiplexer_3_out), .sel(shamt[0]));
  Multiplexer multiplexer_4 (.in0(in_1[5]), .in1(in_1[4]), .out(multiplexer_4_out), .sel(shamt[0]));
  Multiplexer multiplexer_5 (.in0(in_1[4]), .in1(in_1[3]), .out(multiplexer_5_out), .sel(shamt[0]));
  Multiplexer multiplexer_6 (.in0(in_1[3]), .in1(in_1[2]), .out(multiplexer_6_out), .sel(shamt[0]));
  Multiplexer multiplexer_7 (.in0(in_1[2]), .in1(in_1[1]), .out(multiplexer_7_out), .sel(shamt[0]));
  Multiplexer multiplexer_8 (.in0(in_1[1]), .in1(in_1[0]), .out(multiplexer_8_out), .sel(shamt[0]));
  Multiplexer multiplexer_9 (.in0(in_1[0]), .in1(multiplexer_1_out), .out(multiplexer_9_out), .sel(shamt[0]));
  Multiplexer multiplexer_10 (
    .in0(multiplexer_2_out), .in1(multiplexer_4_out), .out(multiplexer_10_out), .sel(shamt[1]));
  Multiplexer multiplexer_11 (
    .in0(multiplexer_3_out), .in1(multiplexer_5_out), .out(multiplexer_11_out), .sel(shamt[1]));
  Multiplexer multiplexer_12 (
    .in0(multiplexer_4_out), .in1(multiplexer_6_out), .out(multiplexer_12_out), .sel(shamt[1]));
  Multiplexer multiplexer_13 (
    .in0(multiplexer_5_out), .in1(multiplexer_7_out), .out(multiplexer_13_out), .sel(shamt[1]));
  Multiplexer multiplexer_14 (
    .in0(multiplexer_6_out), .in1(multiplexer_8_out), .out(multiplexer_14_out), .sel(shamt[1]));
  Multiplexer multiplexer_15 (
    .in0(multiplexer_7_out), .in1(multiplexer_9_out), .out(multiplexer_15_out), .sel(shamt[1]));
  Multiplexer multiplexer_16 (
    .in0(multiplexer_8_out), .in1(multiplexer_1_out), .out(multiplexer_16_out), .sel(shamt[1]));
  Multiplexer multiplexer_17 (
    .in0(multiplexer_9_out), .in1(multiplexer_1_out), .out(multiplexer_17_out), .sel(shamt[1]));
  Multiplexer multiplexer_18 (.in0(multiplexer_10_out), .in1(multiplexer_14_out), .out(out_4[7]), .sel(shamt[2]));
  Multiplexer multiplexer_19 (.in0(multiplexer_11_out), .in1(multiplexer_15_out), .out(out_4[6]), .sel(shamt[2]));
  Multiplexer multiplexer_20 (.in0(multiplexer_12_out), .in1(multiplexer_16_out), .out(out_4[5]), .sel(shamt[2]));
  Multiplexer multiplexer_21 (.in0(multiplexer_13_out), .in1(multiplexer_17_out), .out(out_4[4]), .sel(shamt[2]));
  Multiplexer multiplexer_22 (.in0(multiplexer_14_out), .in1(multiplexer_1_out), .out(out_4[3]), .sel(shamt[2]));
  Multiplexer multiplexer_23 (.in0(multiplexer_15_out), .in1(multiplexer_1_out), .out(out_4[2]), .sel(shamt[2]));
  Multiplexer multiplexer_24 (.in0(multiplexer_16_out), .in1(multiplexer_1_out), .out(out_4[1]), .sel(shamt[2]));
  Multiplexer multiplexer_25 (.in0(multiplexer_17_out), .in1(multiplexer_1_out), .out(out_4[0]), .sel(shamt[2]));
endmodule

module COND (
  input  z,
  input  c,
  input  n,
  input  v,
  input  s,
  input  [2:0] in_6,
  output T
);

  wire and_1_out, multiplexer_1_out, not_1_out, not_2_out, not_3_out, not_4_out, not_5_out, xor_1_out;

  not not_1 (not_1_out, c);
  xor xor_1 (xor_1_out, n, v);
  Multiplexer multiplexer_1 (.in0(not_1_out), .in1(xor_1_out), .out(multiplexer_1_out), .sel(s));
  not not_2 (not_2_out, z);
  not not_3 (not_3_out, multiplexer_1_out);
  and and_1 (and_1_out, not_2_out, not_3_out);
  not not_4 (not_4_out, and_1_out);
  not not_5 (not_5_out, n);
  Multiplexer #(.select(3)) multiplexer_2 (
    .in0(z), .in1(not_2_out), .in2(multiplexer_1_out), .in3(not_3_out), .in4(and_1_out), .in5(not_4_out),
    .in6(n), .in7(not_5_out), .out(T), .sel(in_6));
endmodule

module ALU (
  input  [7:0] A,
  input  [7:0] B,
  input  [2:0] shamt,
  input  [2:0] opcode,
  input  unsign_sign_8fb0702b,
  input  [2:0] COND_0_1NOT_2_3_4_5_6_ve_7_ve_39ad1e93,
  output T,
  output [7:0] result
);

  wire adder_8b_da2f1a56_1_carry, adder_8b_da2f1a56_1_overflow, and_1_out, and_2_out, nor_1_out, not_1_out,
       not_2_out;
  wire [7:0] adder_8b_da2f1a56_1_out_8, and_8b_6958ddab_1_out_3, left_shift_8b_5403b38f_1_out_4,
       or_8b_d5c0bf99_1_out_3, right_shift_8b_d6623a56_1_out_4, xor_8b_18f17b81_1_out_3;

  not not_1 (not_1_out, opcode[1]);
  not not_2 (not_2_out, opcode[2]);
  and and_1 (and_1_out, opcode[0], not_1_out, not_2_out);
  and and_2 (and_2_out, opcode[0], opcode[1], opcode[2]);
  adder_8b_da2f1a56 adder_8b_da2f1a56_1 (
    .A(A), .B(B), .Sub(and_1_out), .out_8(adder_8b_da2f1a56_1_out_8), .Carry(adder_8b_da2f1a56_1_carry),
    .Overflow(adder_8b_da2f1a56_1_overflow));  // open: Zero, L_VE_73f3d2a1
  AND_8b_6958ddab and_8b_6958ddab_1 (.in_1(A), .in_2(B), .out_3(and_8b_6958ddab_1_out_3));
  XOR_8b_18f17b81 xor_8b_18f17b81_1 (.in_1(A), .in_2(B), .out_3(xor_8b_18f17b81_1_out_3));
  OR_8b_d5c0bf99 or_8b_d5c0bf99_1 (.in_1(A), .in_2(B), .out_3(or_8b_d5c0bf99_1_out_3));
  left_shift_8b_5403b38f left_shift_8b_5403b38f_1 (
    .in_1(A), .shamt(shamt), .Arithmetic(and_2_out), .out_4(left_shift_8b_5403b38f_1_out_4));
  right_shift_8b_d6623a56 right_shift_8b_d6623a56_1 (
    .in_1(A), .shamt(shamt), .Arithmetic(and_2_out), .out_4(right_shift_8b_d6623a56_1_out_4));
  Multiplexer #(.select(3), .width(8)) multiplexer_1 (
    .in0(adder_8b_da2f1a56_1_out_8), .in1(adder_8b_da2f1a56_1_out_8), .in2(and_8b_6958ddab_1_out_3),
    .in3(xor_8b_18f17b81_1_out_3), .in4(or_8b_d5c0bf99_1_out_3), .in5(left_shift_8b_5403b38f_1_out_4),
    .in6(right_shift_8b_d6623a56_1_out_4), .in7(right_shift_8b_d6623a56_1_out_4), .out(result), .sel(opcode));
  nor nor_1 (nor_1_out, result[0], result[1], result[2], result[3], result[4], result[5], result[6], result[7]);
  COND cond_1 (
    .s(unsign_sign_8fb0702b), .in_6(COND_0_1NOT_2_3_4_5_6_ve_7_ve_39ad1e93), .z(nor_1_out),
    .c(adder_8b_da2f1a56_1_carry), .n(result[7]), .v(adder_8b_da2f1a56_1_overflow), .T(T));
endmodule

module Register_8b_15525367 (
  input  [7:0] in_1,
  input  Clock,
  input  Wri,
  input  clear,
  output [7:0] out_5
);

  Register register_1 (.D(in_1), .en(Wri), .clk(Clock), .Q(out_5), .clr(clear));
endmodule

module register_file_ff49ba11 (
  input  [7:0] Din,
  input  [2:0] WriAddr,
  input  [2:0] readAddrA,
  input  [2:0] readAddrB,
  input  [7:0] IO,
  input  From_keyBoard,
  input  WriEn,
  input  Clock,
  input  ClearAll,
  output [7:0] DoutA,
  output [7:0] DoutB
);

  wire and_1_out, and_2_out, and_3_out, and_4_out, and_5_out, and_6_out, and_7_out, decoder_1_out1,
       decoder_1_out2, decoder_1_out3, decoder_1_out4, decoder_1_out5, decoder_1_out6, decoder_1_out7;
  wire [7:0] multiplexer_1_out, register_8b_15525367_1_out_5, register_8b_15525367_2_out_5,
       register_8b_15525367_3_out_5, register_8b_15525367_4_out_5, register_8b_15525367_5_out_5,
       register_8b_15525367_6_out_5, register_8b_15525367_7_out_5;

  Decoder #(.enable("false"), .select(3)) decoder_1 (
    .out1(decoder_1_out1), .out2(decoder_1_out2), .out3(decoder_1_out3), .out4(decoder_1_out4),
    .out5(decoder_1_out5), .out6(decoder_1_out6), .out7(decoder_1_out7), .sel(WriAddr));  // open: out0
  and and_1 (and_1_out, decoder_1_out1, WriEn);
  and and_2 (and_2_out, decoder_1_out2, WriEn);
  and and_3 (and_3_out, decoder_1_out3, WriEn);
  and and_4 (and_4_out, decoder_1_out4, WriEn);
  and and_5 (and_5_out, decoder_1_out5, WriEn);
  and and_6 (and_6_out, decoder_1_out6, WriEn);
  Multiplexer #(.width(8)) multiplexer_1 (.in0(Din), .in1(IO), .out(multiplexer_1_out), .sel(From_keyBoard));
  and and_7 (and_7_out, decoder_1_out7, WriEn);
  Register_8b_15525367 register_8b_15525367_1 (
    .clear(ClearAll), .Clock(Clock), .Wri(and_1_out), .in_1(Din), .out_5(register_8b_15525367_1_out_5));
  Register_8b_15525367 register_8b_15525367_2 (
    .clear(ClearAll), .Clock(Clock), .Wri(and_2_out), .in_1(Din), .out_5(register_8b_15525367_2_out_5));
  Register_8b_15525367 register_8b_15525367_3 (
    .clear(ClearAll), .Clock(Clock), .Wri(and_3_out), .in_1(Din), .out_5(register_8b_15525367_3_out_5));
  Register_8b_15525367 register_8b_15525367_4 (
    .clear(ClearAll), .Clock(Clock), .Wri(and_4_out), .in_1(Din), .out_5(register_8b_15525367_4_out_5));
  Register_8b_15525367 register_8b_15525367_5 (
    .clear(ClearAll), .Clock(Clock), .Wri(and_5_out), .in_1(Din), .out_5(register_8b_15525367_5_out_5));
  Register_8b_15525367 register_8b_15525367_6 (
    .clear(ClearAll), .Clock(Clock), .Wri(and_6_out), .in_1(Din), .out_5(register_8b_15525367_6_out_5));
  Register_8b_15525367 register_8b_15525367_7 (
    .clear(ClearAll), .Clock(Clock), .Wri(and_7_out), .in_1(multiplexer_1_out),
    .out_5(register_8b_15525367_7_out_5));
  Multiplexer #(.select(3), .width(8)) multiplexer_2 (
    .in0({8{1'b0}}), .in1(register_8b_15525367_1_out_5), .in2(register_8b_15525367_2_out_5),
    .in3(register_8b_15525367_3_out_5), .in4(register_8b_15525367_4_out_5),
    .in5(register_8b_15525367_5_out_5), .in6(register_8b_15525367_6_out_5),
    .in7(register_8b_15525367_7_out_5), .out(DoutA), .sel(readAddrA));
  Multiplexer #(.select(3), .width(8)) multiplexer_3 (
    .in0({8{1'b0}}), .in1(register_8b_15525367_1_out_5), .in2(register_8b_15525367_2_out_5),
    .in3(register_8b_15525367_3_out_5), .in4(register_8b_15525367_4_out_5),
    .in5(register_8b_15525367_5_out_5), .in6(register_8b_15525367_6_out_5),
    .in7(register_8b_15525367_7_out_5), .out(DoutB), .sel(readAddrB));
endmodule

module PC (
  input  [7:0] offest,
  input  [7:0] Imm,
  input  Jump,
  input  Branch,
  input  Clk,
  input  PC_load_028894c1,
  input  clear,
  input  RET,
  input  JSR,
  output [7:0] out_10
);

  wire or_1_out;
  wire [1:0] or_2_out;
  wire [7:0] adder_8b_da2f1a56_1_out_8, adder_8b_da2f1a56_2_out_8, multiplexer_1_out,
       register_8b_15525367_1_out_5;

  or or_1 (or_1_out, Jump, RET);
  or or_2 (or_2_out[0], Branch, RET);
  adder_8b_da2f1a56 adder_8b_da2f1a56_1 (
    .A(out_10), .B(8'h1), .Sub(1'b0), .out_8(adder_8b_da2f1a56_1_out_8));  // open: Zero, L_VE_73f3d2a1, Carry, Overflow
  adder_8b_da2f1a56 adder_8b_da2f1a56_2 (
    .A(out_10), .B(offest), .Sub(1'b0), .out_8(adder_8b_da2f1a56_2_out_8));  // open: Zero, L_VE_73f3d2a1, Carry, Overflow
  or or_3 (or_2_out[1], JSR, or_1_out);
  Register_8b_15525367 register_8b_15525367_1 (
    .clear(clear), .Clock(Clk), .Wri(JSR), .in_1(adder_8b_da2f1a56_1_out_8),
    .out_5(register_8b_15525367_1_out_5));
  Multiplexer #(.select(2), .width(8)) multiplexer_1 (
    .in0(adder_8b_da2f1a56_1_out_8), .in1(adder_8b_da2f1a56_2_out_8), .in2(Imm),
    .in3(register_8b_15525367_1_out_5), .out(multiplexer_1_out), .sel(or_2_out));
  Register_8b_15525367 register_8b_15525367_2 (
    .clear(clear), .Clock(Clk), .Wri(PC_load_028894c1), .in_1(multiplexer_1_out), .out_5(out_10));
endmodule

module control_unit_13fa0f51 (
  input  [31:0] in_1,
  input  T,
  output Jump,
  output Branch,
  output RET,
  output JSR,
  output PC_load,
  output [2:0] WriAddr,
  output [2:0] ReadAddrA,
  output [2:0] ReadAddrB,
  output WriEn,
  output [2:0] ALU_shamt_1da623f9,
  output [2:0] ALU_opcode_0dd9a30d,
  output UnSigned_Signed_dba66f78,
  output [2:0] COND,
  output [7:0] Imm,
  output is_imm,
  output RAM_Wri,
  output RAM_load,
  output RAM_to_Reg
);

  wire and_2_out, and_3_out, decoder_1_out0, decoder_1_out2, not_1_out, not_2_out, not_3_out, not_4_out,
       not_5_out, not_6_out, not_7_out, not_8_out;

  Decoder #(.enable("false"), .select(3)) decoder_1 (
    .out0(decoder_1_out0), .out1(Jump), .out2(decoder_1_out2), .out3(RET), .out4(JSR), .sel(in_1[5:3]));  // open: out5, out6, out7
  not not_1 (not_1_out, in_1[1]);
  not not_2 (not_2_out, in_1[2]);
  not not_3 (not_3_out, in_1[0]);
  and and_1 (UnSigned_Signed_dba66f78, not_3_out, in_1[1], in_1[2]);
  and and_2 (and_2_out, in_1[2], not_1_out);
  or or_1 (is_imm, and_2_out, and_3_out);
  and and_3 (and_3_out, in_1[0], not_2_out);
  not not_4 (not_4_out, in_1[0]);
  and and_4 (RAM_load, in_1[2], not_4_out, not_5_out);
  not not_5 (not_5_out, in_1[1]);
  not not_6 (not_6_out, in_1[1]);
  and and_5 (RAM_Wri, in_1[0], not_6_out, in_1[2]);
  and and_6 (Branch, decoder_1_out2, T);
  or or_2 (PC_load, JSR, RET, decoder_1_out2, Jump, decoder_1_out0);
  not not_7 (not_7_out, in_1[0]);
  not not_8 (not_8_out, in_1[2]);
  or or_3 (WriEn, not_7_out, not_8_out);

  assign ALU_opcode_0dd9a30d = in_1[19:17];
  assign ALU_shamt_1da623f9 = in_1[22:20];
  assign COND = in_1[16:14];
  assign Imm = in_1[13:6];
  assign RAM_to_Reg = RAM_load;
  assign ReadAddrA = in_1[28:26];
  assign ReadAddrB = in_1[25:23];
  assign WriAddr = in_1[31:29];
endmodule

module displayRAM (
  input  RAM_Wri,
  input  [7:0] Adress,
  input  [7:0] DataB,
  input  clock,
  input  Clear,
  output [7:0] Addr,
  output [7:0] ASCII
);

  wire and_1_out, and_2_out;

  and and_1 (and_1_out, RAM_Wri, and_2_out);
  and and_2 (and_2_out, Adress[0], Adress[1], Adress[2], Adress[3], Adress[5], Adress[6], Adress[7], Adress[4]);
  Counter counter_1 (.D({8{1'b0}}), .count(and_1_out), .Q(Addr), .clk(clock), .clr(Clear));  // open: load, carry, up
  RAM #(.clearpin("true")) ram_1 (
    .addr(Addr), .we(and_1_out), .oe(and_1_out), .clk(clock), .din(DataB), .dout(ASCII), .clr(Clear));
endmodule

module ASCII (
  input  [7:0] in_1,
  output [39:0] out_2
);

  ROM #(.dataWidth(40)) rom_1 (.addr(in_1), .data(out_2));

  // Notes on the sheet:
  //   contents of rom_1 (hex, n*v repeats v):
  //   3a39ace2e 388421184 7e107062e 3a213083f 85f928c2 3a210fa1f 3a31f4107 41041043f 3a317462e 70417c62e
  //   23*0 100421084 294a 295f57d4a 13c5751e4 e6820b38 365545288 410c6 88842082 208210888 12aefbaa4
  //   84f9080 10c600000 f8000 18c000000 20820820 3a39ace2e 388421184 7e107062e 3a213083f 85f928c2
  //   3a210fa1f 3a31f4107 41041043f 3a317462e 70417c62e 401000 208401000 44441041 1f07c00 208208888
  //   10043062e 3e16bd62e 463f8c544 7a31f463e 3a308422e 7a318c63e 7e10f421f 4210f421f 3e338422f 4631fc631
  //   38842108e 324210847 4654c5251 7e1084210 4635ad771 4633ae631 3a318c62e 4210f463e 36558c62e 4654f463e
  //   3a217422e 1084212bf 3a318c631 11518c631 2ab5ac631 462a22a31 108422a31 7e087083f 3d084210f 2222200
  //   3c210842f 4544 7c0000000 1118c 3e4e13000 5b31cda10 3a308b800 36719b421 3a1f8b800 1084710a2 5b39b800
  //   4631cda10 388423004 324210802 4a98a4a10 38842108c 56b5ae800 4631cd800 3a318b800 42d9cd800 5b39b400
  //   4210cd800 782e83c00 8a427c84 36718c400 11518c400 2ab58c400 454454400 442f8c400 7d0417c00 88441082
  //   108401084 208411088 aa8
endmodule

module word (
  input  [39:0] in_1,
  input  Wri,
  input  Clock,
  input  Clear
);

  wire [39:0] register_1_q;

  Register #(.width(40)) register_1 (.D(in_1), .en(Wri), .clk(Clock), .Q(register_1_q), .clr(Clear));
  DotMatrix #(.inputtype("row"), .matrixrows(8)) dotmatrix_1 (
    .row0(register_1_q[4:0]), .row1(register_1_q[9:5]), .row2(register_1_q[14:10]),
    .row3(register_1_q[19:15]), .row4(register_1_q[24:20]), .row5(register_1_q[29:25]),
    .row6(register_1_q[34:30]), .row7(register_1_q[39:35]));
endmodule

module mon (
  input  [39:0] in_1,
  input  [4:0] addr,
  input  Clock,
  input  Clear
);

  wire decoder_1_out0, decoder_1_out1, decoder_1_out2, decoder_1_out3, decoder_1_out4, decoder_1_out5,
       decoder_1_out6, decoder_1_out7, decoder_1_out8, decoder_1_out9, decoder_1_out10, decoder_1_out11,
       decoder_1_out12, decoder_1_out13, decoder_1_out14, decoder_1_out15, decoder_1_out16, decoder_1_out17,
       decoder_1_out18, decoder_1_out19, decoder_1_out20, decoder_1_out21, decoder_1_out22, decoder_1_out23,
       decoder_1_out24, decoder_1_out25, decoder_1_out26, decoder_1_out27, decoder_1_out28, decoder_1_out29,
       decoder_1_out30, decoder_1_out31;

  Decoder #(.enable("false"), .select(5)) decoder_1 (
    .out0(decoder_1_out0), .out1(decoder_1_out1), .out2(decoder_1_out2), .out3(decoder_1_out3),
    .out4(decoder_1_out4), .out5(decoder_1_out5), .out6(decoder_1_out6), .out7(decoder_1_out7),
    .out8(decoder_1_out8), .out9(decoder_1_out9), .out10(decoder_1_out10), .out11(decoder_1_out11),
    .out12(decoder_1_out12), .out13(decoder_1_out13), .out14(decoder_1_out14), .out15(decoder_1_out15),
    .out16(decoder_1_out16), .out17(decoder_1_out17), .out18(decoder_1_out18), .out19(decoder_1_out19),
    .out20(decoder_1_out20), .out21(decoder_1_out21), .out22(decoder_1_out22), .out23(decoder_1_out23),
    .out24(decoder_1_out24), .out25(decoder_1_out25), .out26(decoder_1_out26), .out27(decoder_1_out27),
    .out28(decoder_1_out28), .out29(decoder_1_out29), .out30(decoder_1_out30), .out31(decoder_1_out31),
    .sel(addr));
  word word_1 (.in_1(in_1), .Wri(decoder_1_out0), .Clock(Clock), .Clear(Clear));
  word word_2 (.in_1(in_1), .Wri(decoder_1_out10), .Clock(Clock), .Clear(Clear));
  word word_3 (.in_1(in_1), .Wri(decoder_1_out20), .Clock(Clock), .Clear(Clear));
  word word_4 (.in_1(in_1), .Wri(decoder_1_out30), .Clock(Clock), .Clear(Clear));
  word word_5 (.in_1(in_1), .Wri(decoder_1_out1), .Clock(Clock), .Clear(Clear));
  word word_6 (.in_1(in_1), .Wri(decoder_1_out11), .Clock(Clock), .Clear(Clear));
  word word_7 (.in_1(in_1), .Wri(decoder_1_out21), .Clock(Clock), .Clear(Clear));
  word word_8 (.in_1(in_1), .Wri(decoder_1_out31), .Clock(Clock), .Clear(Clear));
  word word_9 (.in_1(in_1), .Wri(decoder_1_out2), .Clock(Clock), .Clear(Clear));
  word word_10 (.in_1(in_1), .Wri(decoder_1_out12), .Clock(Clock), .Clear(Clear));
  word word_11 (.in_1(in_1), .Wri(decoder_1_out22), .Clock(Clock), .Clear(Clear));
  word word_12 (.in_1(in_1), .Wri(decoder_1_out3), .Clock(Clock), .Clear(Clear));
  word word_13 (.in_1(in_1), .Wri(decoder_1_out13), .Clock(Clock), .Clear(Clear));
  word word_14 (.in_1(in_1), .Wri(decoder_1_out23), .Clock(Clock), .Clear(Clear));
  word word_15 (.in_1(in_1), .Wri(decoder_1_out4), .Clock(Clock), .Clear(Clear));
  word word_16 (.in_1(in_1), .Wri(decoder_1_out14), .Clock(Clock), .Clear(Clear));
  word word_17 (.in_1(in_1), .Wri(decoder_1_out24), .Clock(Clock), .Clear(Clear));
  word word_18 (.in_1(in_1), .Wri(decoder_1_out5), .Clock(Clock), .Clear(Clear));
  word word_19 (.in_1(in_1), .Wri(decoder_1_out15), .Clock(Clock), .Clear(Clear));
  word word_20 (.in_1(in_1), .Wri(decoder_1_out25), .Clock(Clock), .Clear(Clear));
  word word_21 (.in_1(in_1), .Wri(decoder_1_out6), .Clock(Clock), .Clear(Clear));
  word word_22 (.in_1(in_1), .Wri(decoder_1_out16), .Clock(Clock), .Clear(Clear));
  word word_23 (.in_1(in_1), .Wri(decoder_1_out26), .Clock(Clock), .Clear(Clear));
  word word_24 (.in_1(in_1), .Wri(decoder_1_out7), .Clock(Clock), .Clear(Clear));
  word word_25 (.in_1(in_1), .Wri(decoder_1_out17), .Clock(Clock), .Clear(Clear));
  word word_26 (.in_1(in_1), .Wri(decoder_1_out27), .Clock(Clock), .Clear(Clear));
  word word_27 (.in_1(in_1), .Wri(decoder_1_out8), .Clock(Clock), .Clear(Clear));
  word word_28 (.in_1(in_1), .Wri(decoder_1_out18), .Clock(Clock), .Clear(Clear));
  word word_29 (.in_1(in_1), .Wri(decoder_1_out28), .Clock(Clock), .Clear(Clear));
  word word_30 (.in_1(in_1), .Wri(decoder_1_out9), .Clock(Clock), .Clear(Clear));
  word word_31 (.in_1(in_1), .Wri(decoder_1_out19), .Clock(Clock), .Clear(Clear));
  word word_32 (.in_1(in_1), .Wri(decoder_1_out29), .Clock(Clock), .Clear(Clear));
endmodule

module BCD (
  input  i0,
  input  i1,
  input  i2,
  input  i3,
  input  i4,
  input  i5,
  input  i6,
  input  i7,
  input  i8,
  input  i9,
  input  Add,
  input  Sub,
  input  Mul,
  input  Div,
  input  enter,
  input  Clear,
  output [7:0] data,
  output [7:0] addr,
  output is_number,
  output is_operate
);

  wire not_1_out, not_2_out, not_3_out, or_1_out, or_2_out, or_3_out, or_4_out;
  wire [3:0] bit_extender_1_out, bit_extender_2_out, bit_extender_3_out;
  wire [7:0] adder_1_out, adder_2_out, controlled_buffer_1_out, controlled_buffer_11_out,
       controlled_buffer_15_out, multiplier_1_out, multiplier_2_out, register_1_q, register_2_q, register_3_q;

  assign controlled_buffer_1_out = i0 ? {8{1'b0}} : 8'bz;  // Controlled_Buffer controlled_buffer_1
  assign controlled_buffer_1_out = i1 ? 8'h1 : 8'bz;  // Controlled_Buffer controlled_buffer_2
  assign controlled_buffer_1_out = i2 ? 8'h2 : 8'bz;  // Controlled_Buffer controlled_buffer_3
  assign controlled_buffer_1_out = i3 ? 8'h3 : 8'bz;  // Controlled_Buffer controlled_buffer_4
  assign controlled_buffer_1_out = i4 ? 8'h4 : 8'bz;  // Controlled_Buffer controlled_buffer_5
  assign controlled_buffer_1_out = i5 ? 8'h5 : 8'bz;  // Controlled_Buffer controlled_buffer_6
  assign controlled_buffer_1_out = i6 ? 8'h6 : 8'bz;  // Controlled_Buffer controlled_buffer_7
  assign controlled_buffer_1_out = i7 ? 8'h7 : 8'bz;  // Controlled_Buffer controlled_buffer_8
  assign controlled_buffer_1_out = i8 ? 8'h8 : 8'bz;  // Controlled_Buffer controlled_buffer_9
  assign controlled_buffer_1_out = i9 ? 8'h9 : 8'bz;  // Controlled_Buffer controlled_buffer_10
  assign controlled_buffer_11_out = Add ? 8'hfc : 8'bz;  // Controlled_Buffer controlled_buffer_11
  assign controlled_buffer_11_out = Sub ? 8'hfd : 8'bz;  // Controlled_Buffer controlled_buffer_12
  assign controlled_buffer_11_out = Mul ? 8'hfe : 8'bz;  // Controlled_Buffer controlled_buffer_13
  assign controlled_buffer_11_out = Div ? {8{1'b1}} : 8'bz;  // Controlled_Buffer controlled_buffer_14
  Hex_Digit_Display hex_digit_display_1 (.value(bit_extender_1_out));  // open: dp
  Bit_Extender #(.out_width(4), .\type ("zero")) bit_extender_1 (.in(register_3_q), .out(bit_extender_1_out));
  or or_1 (or_1_out, i0, i1, i2, i3, i4, i5, i6, i7, i8, i9);
  or or_2 (or_2_out, Add, Sub, Mul, Div);
  Hex_Digit_Display hex_digit_display_2 (.value(bit_extender_2_out));  // open: dp
  Bit_Extender #(.out_width(4), .\type ("zero")) bit_extender_2 (.in(register_2_q), .out(bit_extender_2_out));
  Register register_1 (.D(controlled_buffer_1_out), .en(1'b1), .Q(register_1_q), .clk(or_1_out), .clr(Clear));
  Register register_2 (.D(register_1_q), .en(1'b1), .Q(register_2_q), .clk(or_1_out), .clr(Clear));
  Hex_Digit_Display hex_digit_display_3 (.value(bit_extender_3_out));  // open: dp
  Bit_Extender #(.out_width(4), .\type ("zero")) bit_extender_3 (.in(register_1_q), .out(bit_extender_3_out));
  Register register_3 (.D(register_2_q), .en(1'b1), .Q(register_3_q), .clk(or_1_out), .clr(Clear));
  Multiplier multiplier_1 (.a(8'h64), .b(register_3_q), .out(multiplier_1_out));  // open: cin, cout
  Adder adder_1 (.a(multiplier_1_out), .b(multiplier_2_out), .out(adder_1_out));  // open: cin, cout
  Multiplier multiplier_2 (.a(8'ha), .b(register_2_q), .out(multiplier_2_out));  // open: cin, cout
  Adder adder_2 (.a(adder_1_out), .b(register_1_q), .out(adder_2_out));  // open: cin, cout
  assign controlled_buffer_15_out = not_1_out ? adder_2_out : 8'bz;  // Controlled_Buffer controlled_buffer_15
  not not_1 (not_1_out, or_2_out);
  assign controlled_buffer_15_out = not_3_out ? controlled_buffer_11_out : 8'bz;  // Controlled_Buffer controlled_buffer_16
  not not_2 (not_2_out, or_2_out);
  Register #(.trigger("high")) register_4 (
    .D(controlled_buffer_15_out), .en(1'b1), .Q(data), .clk(or_3_out), .clr(Clear));
  not not_3 (not_3_out, not_2_out);
  or or_3 (or_3_out, or_2_out, enter);
  or or_4 (or_4_out, or_1_out, or_3_out);
  S_R_Flip_Flop s_r_ff_1 (
    .S(or_1_out), .R(or_2_out), .clk(or_4_out), .Q(is_number), .Qn(is_operate));  // open: reset, preset
  Multiplexer #(.width(8)) multiplexer_1 (.in0(8'hfe), .in1(8'hfd), .out(addr), .sel(is_number));
endmodule

module times10 (
  input  [7:0] in_1,
  output [7:0] out_2
);

  adder_8b_da2f1a56 adder_8b_da2f1a56_1 (
    .A({in_1[4:0], 3'b000}), .B({in_1[6:0], 1'b0}), .Sub(1'b0), .out_8(out_2));  // open: Zero, L_VE_73f3d2a1, Carry, Overflow
endmodule

module analy (
  input  [2:0] Wri_addr,
  input  Wri,
  output true
);

  wire and_1_out;

  and and_1 (and_1_out, Wri_addr[0], Wri_addr[1], Wri_addr[2]);
  and and_2 (true, and_1_out, Wri);
endmodule
